# Fritzing sketch IoT_device_internal_circuit_schematic (saved by Fritzing 0.9.10b)
breadboards: 2

parts:
  D_O_Circuit1 = D.O. Circuit  # not connected
  Mod1 = Atlas Conductivity Circuit  # not connected
  pH_Circuit1 = pH Circuit  # not connected
  Heltec_Wireless_Stick_Lite1 = Heltec Wireless Stick Lite [part_number=HTIT-WSL]
  A1 = tds-sensor-meter-v1.0_1
  M1 = Atlas EZO isolater carrier [package=THT]
  M2 = Atlas EZO isolater carrier [package=THT]
  M3 = Atlas EZO isolater carrier [package=THT]
  R1 = Resistor [tolerance=±5% power=0.25 resistance=10k package=THT]
  R2 = Resistor [tolerance=±5% power=0.25 resistance=10k package=THT]
  R3 = Resistor [tolerance=±5% power=0.25 resistance=10k package=THT]
  R4 = Resistor [tolerance=±5% power=0.25 resistance=10k package=THT]
  R5 = Resistor [tolerance=±5% power=0.25 resistance=10k package=THT]
  Q7 = NPN-Transistor [package="TO92 [THT]"]
  Q8 = NPN-Transistor [package="TO92 [THT]"]
  Q9 = NPN-Transistor [package="TO92 [THT]"]
  Q10 = NPN-Transistor [package="TO92 [THT]"]
  Q5 = PNP-Transistor [package="TO92 [THT]"]

nets:
  N1: Heltec_Wireless_Stick_Lite1.pin_9, R3.Pin_0
  N2: Heltec_Wireless_Stick_Lite1.pin_10, R5.Pin_0
  N3: Heltec_Wireless_Stick_Lite1.pin_12, R1.Pin_0
  N4: Heltec_Wireless_Stick_Lite1.pin_13, R2.Pin_0
  N5: Heltec_Wireless_Stick_Lite1.pin_15, R4.Pin_0
  N6: Heltec_Wireless_Stick_Lite1.pin_17, M1.pin3, M2.pin3, Q7.E, Q8.E, Q9.E, Q10.E
  N7: Heltec_Wireless_Stick_Lite1.pin_18, Heltec_Wireless_Stick_Lite1.pin_22
  N8: Heltec_Wireless_Stick_Lite1.pin_19, M1.pin1, M2.pin1, M3.pin1, M3.pin3, Q5.E
  N9: Heltec_Wireless_Stick_Lite1.pin_24, M1.pin5, M2.pin5, M3.pin5
  N10: Heltec_Wireless_Stick_Lite1.pin_27, M1.pin4, M2.pin4, M3.pin4
  N11: Heltec_Wireless_Stick_Lite1.pin_37, A1.pin1
  N12: A1.pin2, Q5.C
  N13: A1.pin3, Q9.C
  N14: M1.pin2, Q8.C
  N15: M2.pin2, Q10.C
  N16: M3.pin2, Q7.C
  N17: R1.Pin_1, Q7.B
  N18: R2.Pin_1, Q8.B
  N19: R3.Pin_1, Q5.B
  N20: R4.Pin_1, Q10.B
  N21: R5.Pin_1, Q9.B

custom parts:
  Atlas Conductivity Circuit: There is no shortage of temperature probes out there, and the most accurate of all is the platinum RTD probe. But, converting the resistance of platinum to an actual temperature is unusually complicated. Fortunately, the Atlas Scientific EZO-RTD Circuit makes taking high accuracy readings from a platinum RTD probes easy. The EZO-RTD Circuit can work with any class of 2, 3, or 4 wire platinum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
  Heltec Wireless Stick Lite: Wireless Stick Lite is a part of the Heltec LoRa series and incorporates an ESP32-Pico processor, WiFi, LoRa and Bluetooth with an integrated CP2102 USB to serial port interface and onboard SHT1.25 battery interface with integrated lithium battery management system.
  : TDS Meter V1.0 Development Board Water Meter Filter Measuring Water Sensor Module.
  Atlas EZO isolater carrier: This carrier board utilizes the newest isolation technology, giving us the ability to put isolation into smaller footprint circuits. The Electrically isolated EZO™ carrier board is an efficient way to connect to one Atlas Scientific circuit to your CPU, eliminating the need for a bread board and external isolator. The five pins on top are left open for you to decide how to connect it to your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
